# Fritzing sketch PiRobot (saved by Fritzing 0.8.7b)
breadboards: 1

parts:
  M1 = DC Motor
  M2 = DC Motor
  Part1 = L298N
  M3 = DC Motor
  M4 = DC Motor
  Raspberry_Pi_1 = Raspberry Pi 3 [part_number=RPI-3-V1.2]
  BAT1 = 18650 battery holder [package=battery-18650-kit]
  BAT2 = 18650 battery holder [package=battery-18650-kit]
  J1 = Piezo Speaker
  R1 = Photocell (LDR) [package=THT]
  R2 = Photocell (LDR) [package=THT]
  R3 = Resistor [tolerance=±5% resistance=1k package="0805 [SMD]"]
  C3 = Electrolytic Capacitor [capacitance=1µF package="200 mil [THT, electrolytic]"]
  C4 = Electrolytic Capacitor [capacitance=1µF package="200 mil [THT, electrolytic]"]
  R4 = Resistor [tolerance=±5% resistance=1k package="0805 [SMD]"]
  R5 = Resistor [tolerance=±5% resistance=1k package="0805 [SMD]"]
  Part2 = SRF05 Ultrasonic Rangefinder
  U1 = Tri-Color LED SMD [package=led-tricolor-smd]
  U2 = Tri-Color LED SMD [package=led-tricolor-smd]
  U3 = Tri-Color LED SMD [package=led-tricolor-smd]
  U4 = Tri-Color LED SMD [package=led-tricolor-smd]

nets:
  N1: M1.pin_1, M2.pin_1, Part1.MotorB2
  N2: M1.pin_2, M2.pin_2, Part1.MotorB1
  N3: Part1.MotorA1, M3.pin_1, M4.pin_1
  N4: Part1.MotorA2, M3.pin_2, M4.pin_2
  N5: Part1.12V, BAT1.+
  N6: Part1.ENA, Raspberry_Pi_1.GIPO18
  N7: Part1.IN1, Raspberry_Pi_1.GIPO23
  N8: Part1.IN2, Raspberry_Pi_1.GIPO24
  N9: Part1.IN3, Raspberry_Pi_1.GIPO27
  N10: Part1.IN4, Raspberry_Pi_1.GIPO22
  N11: Part1.ENB, Raspberry_Pi_1.GIPO19
  N12: Part1.GND, BAT2.-
  N13: Raspberry_Pi_1.GPIO2, U1.RED, U4.RED
  N14: Raspberry_Pi_1.GIPO10, U1.GRN, U4.GRN
  N15: Raspberry_Pi_1.GIPO5, R1.pin_1, C4.-
  N16: Raspberry_Pi_1.GIPO6, R2.pin_0, C3.-
  N17: Raspberry_Pi_1.GIPO21, Part2.Trig
  N18: Raspberry_Pi_1.GIPO20, R3.Pin_0, R5.Pin_0
  N19: Raspberry_Pi_1.GIPO15, U2.RED, U3.RED
  N20: Raspberry_Pi_1.GIPO14, U2.GRN, U3.GRN
  GND: Raspberry_Pi_1.GND, J1.pin1, C4.+, R4.Pin_1, Part2.GND, U1.A, U2.A, U3.A, U4.A
  5V: Raspberry_Pi_1.5V, J1.pin2, R1.pin_0, R2.pin_1, Part2.VCC
  N21: BAT1.-, BAT2.+
  N22: R3.Pin_1, R4.Pin_0
  N23: R5.Pin_1, Part2.Echo

notes:
  Front Right
  Motor
  Front Left
  Back Right
  Back Left
  Buzzer
  Left of the car
  Right of the car
  1µF
  1kΩ each
  Front left
  Back left
  Back right
  Front right
  10000mAh Powerbank

custom parts:
  18650 battery holder: 18650 Battery Holder
